# Fritzing sketch WeatherStation (saved by Fritzing 0.8.5b)
breadboards: 1

parts:
  DHT_22 = DHT22 Humidity and Temperature Sensor
  Raspberry_Pi = Raspberry Pi (Model B)
  R1 = Resistor [tolerance=±5% resistance=10k package=THT]
  BMP180 = BMP085 Breakout

nets:
  VDD: DHT_22.VDD, Raspberry_Pi.3V3, R1.Pin_0, BMP180.VIN
  N1: DHT_22.DATA, Raspberry_Pi.#17, R1.Pin_1
  GND: DHT_22.GND, Raspberry_Pi.GND, BMP180.GND
  N2: Raspberry_Pi.SDA, BMP180.SDA
  N3: Raspberry_Pi.SCL, BMP180.SCL

custom parts:
  Raspberry Pi (Model B): Raspberry Pi Single-board Computer, Model B
  BMP085 Breakout: A breakout for the BMP085 barometric pressure and temperature sensor
